# Fritzing sketch Disorgan Schematic (saved by Fritzing 0.9.9b)
breadboards: 1

parts:
  R1 = Resistor [tolerance=±5% resistance=14.87k power=0.25 package=THT]
  C1 = Ceramic Capacitor [capacitance=470nF voltage=35V package="200 mil [THT, multilayer]"]
  R2 = Resistor [tolerance=±5% resistance=14.87k power=0.25 package=THT]
  C2 = Ceramic Capacitor [capacitance="100 nF" voltage=35V package="200 mil [THT, multilayer]"]
  J3 = Infrared Proximity Sensor
  J4 = Infrared Proximity Sensor
  J5 = Infrared Proximity Sensor
  J6 = Infrared Proximity Sensor
  J7 = Infrared Proximity Sensor
  J8 = Infrared Proximity Sensor
  R3 = Resistor [tolerance=±5% resistance=14.87k power=0.25 package=THT]
  C4 = Ceramic Capacitor [capacitance="100 nF" voltage=35V package="200 mil [THT, multilayer]"]
  R4 = Resistor [tolerance=±5% resistance=14.87k power=0.25 package=THT]
  C5 = Ceramic Capacitor [capacitance="100 nF" voltage=35V package="200 mil [THT, multilayer]"]
  R5 = Resistor [tolerance=±5% resistance=14.87k power=0.25 package=THT]
  C6 = Ceramic Capacitor [capacitance="100 nF" voltage=35V package="200 mil [THT, multilayer]"]
  R6 = Resistor [tolerance=±5% resistance=14.87k power=0.25 package=THT]
  C7 = Ceramic Capacitor [capacitance="100 nF" voltage=35V package="200 mil [THT, multilayer]"]
  R10 = Slide Potentiometer [maximum_resistance=100kΩ]
  R11 = Slide Potentiometer [maximum_resistance=100kΩ]
  R12 = Slide Potentiometer [maximum_resistance=100kΩ]
  R13 = Slide Potentiometer [maximum_resistance=100kΩ]
  R14 = Slide Potentiometer [maximum_resistance=100kΩ]
  R15 = Slide Potentiometer [maximum_resistance=100kΩ]
  C8 = Capacitor Polarized [package=cpol-radial-100uf-25v]
  Componente2 = Arduino Micro (Rev3)  # not connected

nets:
  N1: R1.Pin_0, C1.0
  N2: R1.Pin_1, J3.Vout
  GND: C1.1, C2.1, J3.GND, J4.GND, J5.GND, J6.GND, J7.GND, J8.GND, C4.1, C5.1, C6.1, C7.1, R10.leg2, R11.leg2, R12.leg2, R13.leg2, R14.leg2, R15.leg2, C8.-
  N3: R2.Pin_0, C2.0
  N4: R2.Pin_1, J4.Vout
  VCC: J3.Vcc, J4.Vcc, J5.Vcc, J6.Vcc, J7.Vcc, J8.Vcc, R10.leg1, R11.leg1, R12.leg1, R13.leg1, R14.leg1, R15.leg1, C8.+
  N5: J5.Vout, R4.Pin_1
  N6: J6.Vout, R3.Pin_1
  N7: J7.Vout, R6.Pin_1
  N8: J8.Vout, R5.Pin_1
  N9: R3.Pin_0, C4.0
  N10: R4.Pin_0, C5.0
  N11: R5.Pin_0, C6.0
  N12: R6.Pin_0, C7.0

notes:
  15k Ohm Resistor
  Sharp GP2Y0A41SK0F
  Arduino Micro
  Slide potentiometers pins
  1 = gnd
  2 = wiper
  3 = 5v
  Electrolytic capacitor
  47uF
  Ceramic Capacitor 1 uF

custom parts:
  Arduino Micro (Rev3): The Arduino Micro is a microcontroller board based on the ATmega32u4 (datasheet), developed in conjunction with Adafruit. It has 20 digital input/output pins (of which 7 can be used as PWM outputs and 12 as analog inputs), a 16 MHz crystal oscillator, a micro USB connection, an ICSP header, and a reset button. It contains everything needed to support the microcontroller; simply connect it to a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
